# Fritzing sketch schmatic (saved by Fritzing 1.0.8)
breadboards: 2

parts:
  A1 = BMI160 breakout
  MH-ET_LIVE_ESP32_DEVKIT1 = MH-ET LIVE ESP32 DEVKIT 38 pins
  J1 = Piezo Speaker

nets:
  N1: A1.Pin_9, MH-ET_LIVE_ESP32_DEVKIT1.IO21
  N2: A1.Pin_10, MH-ET_LIVE_ESP32_DEVKIT1.IO22
  N3: A1.Pin_11, MH-ET_LIVE_ESP32_DEVKIT1.GND#64
  N4: A1.Pin_12, MH-ET_LIVE_ESP32_DEVKIT1.3V3
  N5: MH-ET_LIVE_ESP32_DEVKIT1.IO19, J1.pin1

custom parts:
  BMI160 breakout: BMI160 Latest Stance Accelerometer Gyroscope module 6 Dof inertial Measurement Sensors.
  MH-ET LIVE ESP32 DEVKIT 38 pins: http://mh.nodebb.com/topic/2/mh-et-live-esp32-devkit
